# Fritzing sketch hardware (saved by Fritzing 0.9.9b)
breadboards: 1

parts:
  Componente1 = Arduino Uno (Rev3)
  Componente3 = Adafruit MiCS-5524 Gas Sensor [part_number="Adafruit #3199"]
  DHT2 = DHT11 Humitidy and Temperature Sensor
  HC-SR04_Sensor_1 = HC-SR04 Ultrasonic Distance Sensor
  HC-SR04_Sensor_2 = HC-SR04 Ultrasonic Distance Sensor
  Mod1 = Raspberry Pi 4B  # not connected
  BAT1 = BC9VPC [package=bc9vpc]
  M1 = gear-motor
  M2 = gear-motor
  IC1 = L293D [package=THT]
  CAMERA1 = TTL Serial JPEG Camera  # not connected
  CAMERA2 = TTL Serial JPEG Camera  # not connected

nets:
  N1: Componente1.A0, Componente3.AOUT
  N2: Componente1.D8, IC1.In_2
  N3: Componente1.D9_PWM, IC1.Enable_1
  N4: Componente1.D10_PWM/SS, M1.pin_1, IC1.Out_4_(_Controlled_by_Enable_2_)
  N5: Componente1.D11_PWM/MOSI, HC-SR04_Sensor_2.ECHO
  N6: Componente1.D12/MISO, HC-SR04_Sensor_2.TRIG
  N7: Componente1.D13/SCK, IC1.In_3
  N8: Componente1.D2, DHT2.DATA
  N9: Componente1.D3_PWM, HC-SR04_Sensor_1.ECHO
  N10: Componente1.D4, Componente3.ENABLE
  N11: Componente1.D5_PWM, IC1.In_1
  N12: Componente1.D6_PWM, IC1.Enable_2
  N13: Componente1.D7, HC-SR04_Sensor_1.TRIG
  VCC: Componente1.5V, Componente3.5.0V, DHT2.VDD, HC-SR04_Sensor_1.VCC, HC-SR04_Sensor_2.VCC
  GND: Componente1.GND, Componente3.GND, HC-SR04_Sensor_1.GND, HC-SR04_Sensor_2.GND
  N14: DHT2.GND, BAT1.V-, IC1.0V
  N15: BAT1.V+, IC1.+Vmotor, IC1.+V
  N16: M1.pin_2, IC1.Out_3_(_Controlled_by_Enable_2_)
  N17: M2.pin_1, IC1.Out_2_(_Controlled_by_Enable_1_)
  N18: M2.pin_2, IC1.Out_1_(_Controlled_by_Enable_1_)

custom parts:
  Adafruit MiCS-5524 Gas Sensor: Give your next sensor project a nose for gasses with the Adafruit MiCS-5524 Gas Sensor Breakout. This breakout makes it easy to use this nice sensor from SGX Sensortech. The MiCS-5524 is a robust MEMS sensor for indoor carbon monoxide and natural gas leakage detection, it's suitable also for indoor air quality monitoring; breath checker and early fire detection. Please note: This sensor is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
  DHT11 Humitidy and Temperature Sensor: DHT11 Humidity and Temperature Sensor
  TTL Serial JPEG Camera: TTL Serial JPEG Camera with NTSC Out
